// Logisim project Schematic.circ as structural Verilog: 11 circuits, main circuit SAP-1
module SAP_1 (
  input  in_1,
  output out_2,
  output out_3,
  output out_4,
  output out_5,
  output out_6,
  output out_7,
  output out_8,
  output out_9
);

  wire Clear, Clock, clock_1_out;
  wire [3:0] IR_CON, MAR_ROM;
  wire [7:0] ALU_A, ALU_B, Bus;
  wire [11:0] Control_Word;

  CON con_1 (
    .CLK(Clock), .CLR(Clear), .I3(IR_CON[3]), .I2(IR_CON[2]), .I1(IR_CON[1]), .I0(IR_CON[0]),
    .Clock(clock_1_out), .Clear(in_1), .Count_PC(Control_Word[11]), .Enable_PC(Control_Word[10]),
    .Load_MAR(Control_Word[9]), .Enable_ROM(Control_Word[8]), .Load_IR(Control_Word[7]),
    .Enable_IR(Control_Word[6]), .Load_A(Control_Word[5]), .Enable_A(Control_Word[4]),
    .Subtract(Control_Word[3]), .Enable_ALU(Control_Word[2]), .Load_B(Control_Word[1]),
    .Load_O(Control_Word[0]));
  Clock clock_1 (.out(clock_1_out));
  PC pc_1 (
    .C(Control_Word[11]), .CLK(Clock), .CLR(Clear), .O3(Bus[3]), .O2(Bus[2]), .O1(Bus[1]), .O0(Bus[0]),
    .E(Control_Word[10]));
  MAR mar_1 (
    .I3(Bus[3]), .I2(Bus[2]), .I1(Bus[1]), .I0(Bus[0]), .L(Control_Word[9]), .CLK(Clock), .O3(MAR_ROM[3]),
    .O2(MAR_ROM[2]), .O1(MAR_ROM[1]), .O0(MAR_ROM[0]), .CLR(Clear));
  ROM rom_1 (
    .A3(MAR_ROM[3]), .A2(MAR_ROM[2]), .A1(MAR_ROM[1]), .A0(MAR_ROM[0]), .O7(Bus[7]), .O6(Bus[6]),
    .O5(Bus[5]), .O4(Bus[4]), .O3(Bus[3]), .O2(Bus[2]), .O1(Bus[1]), .O0(Bus[0]), .E(Control_Word[8]));
  IR ir_1 (
    .CLK(Clock), .CLR(Clear), .O4(IR_CON[0]), .O5(IR_CON[1]), .O6(IR_CON[2]), .O7(IR_CON[3]), .O3(Bus[3]),
    .O2(Bus[2]), .O1(Bus[1]), .O0(Bus[0]), .E(Control_Word[6]), .I7(Bus[7]), .I6(Bus[6]), .I5(Bus[5]),
    .I4(Bus[4]), .I3(Bus[3]), .I2(Bus[2]), .I1(Bus[1]), .I0(Bus[0]), .L(Control_Word[7]));
  A a_1 (
    .I7(Bus[7]), .I6(Bus[6]), .I5(Bus[5]), .I4(Bus[4]), .I3(Bus[3]), .I2(Bus[2]), .I1(Bus[1]), .I0(Bus[0]),
    .L(Control_Word[5]), .CLK(Clock), .O7(Bus[7]), .O6(Bus[6]), .O5(Bus[5]), .O4(Bus[4]),
    .E(Control_Word[4]), .O3(Bus[3]), .O2(Bus[2]), .O1(Bus[1]), .O0(Bus[0]), .R7(ALU_A[7]), .R6(ALU_A[6]),
    .R5(ALU_A[5]), .R4(ALU_A[4]), .R3(ALU_A[3]), .R2(ALU_A[2]), .R1(ALU_A[1]), .R0(ALU_A[0]), .CLR(Clear));
  ALU alu_1 (
    .A7(ALU_A[7]), .A6(ALU_A[6]), .A5(ALU_A[5]), .A4(ALU_A[4]), .A3(ALU_A[3]), .A2(ALU_A[2]), .A1(ALU_A[1]),
    .A0(ALU_A[0]), .B7(ALU_B[7]), .B6(ALU_B[6]), .B5(ALU_B[5]), .B4(ALU_B[4]), .B3(ALU_B[3]), .B2(ALU_B[2]),
    .B1(ALU_B[1]), .B0(ALU_B[0]), .S(Control_Word[3]), .E(Control_Word[2]), .O7(Bus[7]), .O6(Bus[6]),
    .O5(Bus[5]), .O4(Bus[4]), .O3(Bus[3]), .O2(Bus[2]), .O1(Bus[1]), .O0(Bus[0]));
  B b_1 (
    .I7(Bus[7]), .I6(Bus[6]), .I5(Bus[5]), .I4(Bus[4]), .I3(Bus[3]), .I2(Bus[2]), .I1(Bus[1]), .I0(Bus[0]),
    .L(Control_Word[1]), .CLK(Clock), .O7(ALU_B[7]), .O6(ALU_B[6]), .O5(ALU_B[5]), .O4(ALU_B[4]),
    .O3(ALU_B[3]), .O2(ALU_B[2]), .O1(ALU_B[1]), .O0(ALU_B[0]), .CLR(Clear));
  O o_1 (
    .I7(Bus[7]), .I6(Bus[6]), .I5(Bus[5]), .I4(Bus[4]), .I3(Bus[3]), .I2(Bus[2]), .I1(Bus[1]), .I0(Bus[0]),
    .L(Control_Word[0]), .CLK(Clock), .O7(out_2), .O6(out_3), .O5(out_4), .O4(out_5), .O3(out_6), .O2(out_7),
    .O1(out_8), .O0(out_9), .CLR(Clear));

  // Other names for the same wires on the sheet: Display[7:0] = {out_2, out_3, out_4, out_5, out_6, out_7, out_8, out_9}
endmodule

module ALU (
  input  A7,
  input  A6,
  input  A5,
  input  A4,
  input  A3,
  input  A2,
  input  A1,
  input  A0,
  input  B7,
  input  B6,
  input  B5,
  input  B4,
  input  B3,
  input  B2,
  input  B1,
  input  B0,
  input  S,
  input  E,
  output O7,
  output O6,
  output O5,
  output O4,
  output O3,
  output O2,
  output O1,
  output O0
);

  wire and_1_out, and_2_out, and_3_out, and_4_out, and_5_out, and_6_out, and_7_out, and_8_out, and_9_out,
       and_10_out, and_11_out, and_12_out, and_13_out, and_14_out, and_15_out, and_16_out, and_17_out,
       and_18_out, and_19_out, and_20_out, and_21_out, and_22_out, and_23_out, and_24_out, or_1_out,
       or_2_out, or_3_out, or_4_out, or_5_out, or_6_out, or_7_out, or_8_out, xor_1_out, xor_2_out, xor_3_out,
       xor_4_out, xor_5_out, xor_6_out, xor_7_out, xor_8_out, xor_9_out, xor_10_out, xor_11_out, xor_12_out,
       xor_13_out, xor_14_out, xor_15_out, xor_16_out;

  xor xor_1 (xor_1_out, B0, S);
  xor xor_2 (xor_2_out, B1, S);
  xor xor_3 (xor_3_out, B2, S);
  xor xor_4 (xor_4_out, B3, S);
  xor xor_5 (xor_5_out, B4, S);
  xor xor_6 (xor_6_out, B5, S);
  xor xor_7 (xor_7_out, B6, S);
  xor xor_8 (xor_8_out, B7, S);
  and and_1 (and_1_out, xor_1_out, A0);
  and and_2 (and_2_out, xor_1_out, S);
  or or_1 (or_1_out, and_1_out, and_2_out, and_17_out);
  and and_3 (and_3_out, xor_2_out, or_1_out);
  and and_4 (and_4_out, xor_2_out, A1);
  or or_2 (or_2_out, and_4_out, and_3_out, and_18_out);
  and and_5 (and_5_out, xor_3_out, or_2_out);
  and and_6 (and_6_out, xor_3_out, A2);
  or or_3 (or_3_out, and_6_out, and_5_out, and_19_out);
  and and_7 (and_7_out, xor_4_out, A3);
  and and_8 (and_8_out, xor_4_out, or_3_out);
  or or_4 (or_4_out, and_7_out, and_8_out, and_20_out);
  and and_9 (and_9_out, xor_5_out, or_4_out);
  and and_10 (and_10_out, xor_5_out, A4);
  or or_5 (or_5_out, and_10_out, and_9_out, and_21_out);
  and and_11 (and_11_out, xor_6_out, or_5_out);
  and and_12 (and_12_out, xor_6_out, A5);
  or or_6 (or_6_out, and_12_out, and_11_out, and_22_out);
  and and_13 (and_13_out, xor_7_out, A6);
  and and_14 (and_14_out, xor_7_out, or_6_out);
  or or_7 (or_7_out, and_13_out, and_14_out, and_23_out);
  and and_15 (and_15_out, xor_8_out, A7);
  and and_16 (and_16_out, xor_8_out, or_7_out);
  or or_8 (or_8_out, and_15_out, and_16_out, and_24_out);
  and and_17 (and_17_out, A0, S);
  and and_18 (and_18_out, A1, or_1_out);
  and and_19 (and_19_out, A2, or_2_out);
  and and_20 (and_20_out, A3, or_3_out);
  and and_21 (and_21_out, A4, or_4_out);
  and and_22 (and_22_out, A5, or_5_out);
  and and_23 (and_23_out, A6, or_6_out);
  and and_24 (and_24_out, A7, or_7_out);
  assign O7 = E ? xor_16_out : 1'bz;  // Controlled_Buffer controlled_buffer_1
  xor xor_9 (xor_9_out, S, A0, xor_1_out);
  xor xor_10 (xor_10_out, or_1_out, A1, xor_2_out);
  xor xor_11 (xor_11_out, or_2_out, A2, xor_3_out);
  xor xor_12 (xor_12_out, or_3_out, A3, xor_4_out);
  xor xor_13 (xor_13_out, or_4_out, A4, xor_5_out);
  xor xor_14 (xor_14_out, or_5_out, A5, xor_6_out);
  xor xor_15 (xor_15_out, or_6_out, A6, xor_7_out);
  xor xor_16 (xor_16_out, or_7_out, A7, xor_8_out);
  assign O6 = E ? xor_15_out : 1'bz;  // Controlled_Buffer controlled_buffer_2
  assign O5 = E ? xor_14_out : 1'bz;  // Controlled_Buffer controlled_buffer_3
  assign O4 = E ? xor_13_out : 1'bz;  // Controlled_Buffer controlled_buffer_4
  assign O3 = E ? xor_12_out : 1'bz;  // Controlled_Buffer controlled_buffer_5
  assign O2 = E ? xor_11_out : 1'bz;  // Controlled_Buffer controlled_buffer_6
  assign O0 = E ? xor_9_out : 1'bz;  // Controlled_Buffer controlled_buffer_7
  assign O1 = E ? xor_10_out : 1'bz;  // Controlled_Buffer controlled_buffer_8
endmodule

module A (
  input  I7,
  input  I6,
  input  I5,
  input  I4,
  input  I3,
  input  I2,
  input  I1,
  input  I0,
  input  L,
  input  CLK,
  input  CLR,
  input  E,
  output R7,
  output O7,
  output R6,
  output O6,
  output R5,
  output O5,
  output R4,
  output O4,
  output R3,
  output O3,
  output R2,
  output O2,
  output R1,
  output O1,
  output R0,
  output O0
);

  wire and_1_out, and_2_out, and_3_out, and_4_out, and_5_out, and_6_out, and_7_out, and_8_out, and_9_out,
       and_10_out, and_11_out, and_12_out, and_13_out, and_14_out, and_15_out, and_16_out, not_1_out,
       or_1_out, or_2_out, or_3_out, or_4_out, or_5_out, or_6_out, or_7_out, or_8_out;

  and and_1 (and_1_out, L, I7);
  and and_2 (and_2_out, not_1_out, R7);
  or or_1 (or_1_out, and_1_out, and_2_out);
  and and_3 (and_3_out, not_1_out, R6);
  and and_4 (and_4_out, L, I6);
  or or_2 (or_2_out, and_4_out, and_3_out);
  D_Flip_Flop d_ff_1 (.clk(CLK), .D(or_1_out), .Q(R7), .reset(CLR));  // open: Qn, preset, en
  assign O7 = E ? R7 : 1'bz;  // Controlled_Buffer controlled_buffer_1
  and and_5 (and_5_out, not_1_out, R5);
  and and_6 (and_6_out, L, I5);
  or or_3 (or_3_out, and_6_out, and_5_out);
  D_Flip_Flop d_ff_2 (.clk(CLK), .D(or_2_out), .Q(R6), .reset(CLR));  // open: Qn, preset, en
  assign O6 = E ? R6 : 1'bz;  // Controlled_Buffer controlled_buffer_2
  and and_7 (and_7_out, L, I4);
  and and_8 (and_8_out, not_1_out, R4);
  or or_4 (or_4_out, and_7_out, and_8_out);
  D_Flip_Flop d_ff_3 (.clk(CLK), .D(or_3_out), .Q(R5), .reset(CLR));  // open: Qn, preset, en
  assign O5 = E ? R5 : 1'bz;  // Controlled_Buffer controlled_buffer_3
  and and_9 (and_9_out, not_1_out, R3);
  and and_10 (and_10_out, L, I3);
  or or_5 (or_5_out, and_10_out, and_9_out);
  D_Flip_Flop d_ff_4 (.clk(CLK), .D(or_4_out), .Q(R4), .reset(CLR));  // open: Qn, preset, en
  assign O4 = E ? R4 : 1'bz;  // Controlled_Buffer controlled_buffer_4
  and and_11 (and_11_out, L, I2);
  and and_12 (and_12_out, not_1_out, R2);
  or or_6 (or_6_out, and_11_out, and_12_out);
  D_Flip_Flop d_ff_5 (.clk(CLK), .D(or_5_out), .Q(R3), .reset(CLR));  // open: Qn, preset, en
  assign O3 = E ? R3 : 1'bz;  // Controlled_Buffer controlled_buffer_5
  and and_13 (and_13_out, not_1_out, R1);
  and and_14 (and_14_out, L, I1);
  or or_7 (or_7_out, and_14_out, and_13_out);
  D_Flip_Flop d_ff_6 (.clk(CLK), .D(or_6_out), .Q(R2), .reset(CLR));  // open: Qn, preset, en
  assign O2 = E ? R2 : 1'bz;  // Controlled_Buffer controlled_buffer_6
  and and_15 (and_15_out, L, I0);
  and and_16 (and_16_out, not_1_out, R0);
  or or_8 (or_8_out, and_15_out, and_16_out);
  D_Flip_Flop d_ff_7 (.clk(CLK), .D(or_7_out), .Q(R1), .reset(CLR));  // open: Qn, preset, en
  assign O1 = E ? R1 : 1'bz;  // Controlled_Buffer controlled_buffer_7
  not not_1 (not_1_out, L);
  D_Flip_Flop d_ff_8 (.clk(CLK), .D(or_8_out), .Q(R0), .reset(CLR));  // open: Qn, preset, en
  assign O0 = E ? R0 : 1'bz;  // Controlled_Buffer controlled_buffer_8
endmodule

module B (
  input  I7,
  input  I6,
  input  I5,
  input  I4,
  input  I3,
  input  I2,
  input  I1,
  input  I0,
  input  L,
  input  CLK,
  input  CLR,
  output O7,
  output O6,
  output O5,
  output O4,
  output O3,
  output O2,
  output O1,
  output O0
);

  wire and_1_out, and_2_out, and_3_out, and_4_out, and_5_out, and_6_out, and_7_out, and_8_out, and_9_out,
       and_10_out, and_11_out, and_12_out, and_13_out, and_14_out, and_15_out, and_16_out, not_1_out,
       or_1_out, or_2_out, or_3_out, or_4_out, or_5_out, or_6_out, or_7_out, or_8_out;

  and and_1 (and_1_out, L, I7);
  and and_2 (and_2_out, not_1_out, O7);
  or or_1 (or_1_out, and_1_out, and_2_out);
  and and_3 (and_3_out, not_1_out, O6);
  and and_4 (and_4_out, L, I6);
  or or_2 (or_2_out, and_4_out, and_3_out);
  D_Flip_Flop d_ff_1 (.clk(CLK), .D(or_1_out), .Q(O7), .reset(CLR));  // open: Qn, preset, en
  and and_5 (and_5_out, not_1_out, O5);
  and and_6 (and_6_out, L, I5);
  or or_3 (or_3_out, and_6_out, and_5_out);
  D_Flip_Flop d_ff_2 (.clk(CLK), .D(or_2_out), .Q(O6), .reset(CLR));  // open: Qn, preset, en
  and and_7 (and_7_out, L, I4);
  and and_8 (and_8_out, not_1_out, O4);
  or or_4 (or_4_out, and_7_out, and_8_out);
  D_Flip_Flop d_ff_3 (.clk(CLK), .D(or_3_out), .Q(O5), .reset(CLR));  // open: Qn, preset, en
  and and_9 (and_9_out, L, I3);
  and and_10 (and_10_out, not_1_out, O3);
  or or_5 (or_5_out, and_9_out, and_10_out);
  D_Flip_Flop d_ff_4 (.clk(CLK), .D(or_4_out), .Q(O4), .reset(CLR));  // open: Qn, preset, en
  and and_11 (and_11_out, not_1_out, O2);
  and and_12 (and_12_out, L, I2);
  or or_6 (or_6_out, and_12_out, and_11_out);
  D_Flip_Flop d_ff_5 (.clk(CLK), .D(or_5_out), .Q(O3), .reset(CLR));  // open: Qn, preset, en
  and and_13 (and_13_out, L, I1);
  and and_14 (and_14_out, not_1_out, O1);
  or or_7 (or_7_out, and_13_out, and_14_out);
  D_Flip_Flop d_ff_6 (.clk(CLK), .D(or_6_out), .Q(O2), .reset(CLR));  // open: Qn, preset, en
  and and_15 (and_15_out, L, I0);
  and and_16 (and_16_out, not_1_out, O0);
  or or_8 (or_8_out, and_15_out, and_16_out);
  D_Flip_Flop d_ff_7 (.clk(CLK), .D(or_7_out), .Q(O1), .reset(CLR));  // open: Qn, preset, en
  not not_1 (not_1_out, L);
  D_Flip_Flop d_ff_8 (.clk(CLK), .D(or_8_out), .Q(O0), .reset(CLR));  // open: Qn, preset, en
endmodule

module O (
  input  I7,
  input  I6,
  input  I5,
  input  I4,
  input  I3,
  input  I2,
  input  I1,
  input  I0,
  input  L,
  input  CLK,
  input  CLR,
  output O7,
  output O6,
  output O5,
  output O4,
  output O3,
  output O2,
  output O1,
  output O0
);

  wire and_1_out, and_2_out, and_3_out, and_4_out, and_5_out, and_6_out, and_7_out, and_8_out, and_9_out,
       and_10_out, and_11_out, and_12_out, and_13_out, and_14_out, and_15_out, and_16_out, not_1_out,
       or_1_out, or_2_out, or_3_out, or_4_out, or_5_out, or_6_out, or_7_out, or_8_out;

  and and_1 (and_1_out, not_1_out, O7);
  and and_2 (and_2_out, L, I7);
  or or_1 (or_1_out, and_2_out, and_1_out);
  and and_3 (and_3_out, not_1_out, O6);
  and and_4 (and_4_out, L, I6);
  or or_2 (or_2_out, and_4_out, and_3_out);
  D_Flip_Flop d_ff_1 (.clk(CLK), .D(or_1_out), .Q(O7), .reset(CLR));  // open: Qn, preset, en
  and and_5 (and_5_out, L, I5);
  and and_6 (and_6_out, not_1_out, O5);
  or or_3 (or_3_out, and_5_out, and_6_out);
  D_Flip_Flop d_ff_2 (.clk(CLK), .D(or_2_out), .Q(O6), .reset(CLR));  // open: Qn, preset, en
  and and_7 (and_7_out, L, I4);
  and and_8 (and_8_out, not_1_out, O4);
  or or_4 (or_4_out, and_7_out, and_8_out);
  D_Flip_Flop d_ff_3 (.clk(CLK), .D(or_3_out), .Q(O5), .reset(CLR));  // open: Qn, preset, en
  and and_9 (and_9_out, not_1_out, O3);
  and and_10 (and_10_out, L, I3);
  or or_5 (or_5_out, and_10_out, and_9_out);
  D_Flip_Flop d_ff_4 (.clk(CLK), .D(or_4_out), .Q(O4), .reset(CLR));  // open: Qn, preset, en
  and and_11 (and_11_out, L, I2);
  and and_12 (and_12_out, not_1_out, O2);
  or or_6 (or_6_out, and_11_out, and_12_out);
  D_Flip_Flop d_ff_5 (.clk(CLK), .D(or_5_out), .Q(O3), .reset(CLR));  // open: Qn, preset, en
  and and_13 (and_13_out, L, I1);
  and and_14 (and_14_out, not_1_out, O1);
  or or_7 (or_7_out, and_13_out, and_14_out);
  D_Flip_Flop d_ff_6 (.clk(CLK), .D(or_6_out), .Q(O2), .reset(CLR));  // open: Qn, preset, en
  and and_15 (and_15_out, not_1_out, O0);
  and and_16 (and_16_out, L, I0);
  or or_8 (or_8_out, and_16_out, and_15_out);
  D_Flip_Flop d_ff_7 (.clk(CLK), .D(or_7_out), .Q(O1), .reset(CLR));  // open: Qn, preset, en
  not not_1 (not_1_out, L);
  D_Flip_Flop d_ff_8 (.clk(CLK), .D(or_8_out), .Q(O0), .reset(CLR));  // open: Qn, preset, en
endmodule

module CON (
  input  Clock,
  input  Clear,
  input  I3,
  input  I2,
  input  I1,
  input  I0,
  output CLK,
  output CLR,
  output Enable_PC,
  output Load_MAR,
  output Enable_ROM,
  output Load_IR,
  output Enable_IR,
  output Load_A,
  output Subtract,
  output Enable_ALU,
  output Load_B,
  output Load_O,
  output Count_PC,
  output Enable_A
);

  wire _1_out, _2_out, _3_out, _4_out, _5_out, _6_out, _7_out, _8_out, _9_out, _10_out, _11_out, _12_out,
       _15_out, _16_out, _17_out, _18_out, ADD_out, HLT_out, LDA_out, not_1_out, not_2_out, not_3_out,
       not_4_out, OUT_out, ring_counter_1_o3, ring_counter_1_o4, ring_counter_1_o5, SUB_out;

  not not_1 (not_1_out, I3);
  not not_2 (not_2_out, I2);
  not not_3 (not_3_out, I1);
  not not_4 (not_4_out, I0);
  and LDA (LDA_out, not_4_out, not_3_out, not_2_out, not_1_out);
  and ADD (ADD_out, I0, not_3_out, not_2_out, not_1_out);
  and SUB (SUB_out, not_4_out, I1, not_2_out, not_1_out);
  and OUT (OUT_out, not_4_out, I1, I2, I3);
  and HLT (HLT_out, I0, I1, I2, I3);
  Ring_Counter ring_counter_1 (
    .CLK(CLK), .CLR(Clear), .O5(ring_counter_1_o5), .O4(ring_counter_1_o4), .O3(ring_counter_1_o3),
    .O2(Count_PC), .O1(Load_IR), .O0(Enable_PC));
  and and_1 (CLK, ~HLT_out, Clock);  // AND_Gate
  and _2 (_2_out, ADD_out, ring_counter_1_o3);
  and _1 (_1_out, LDA_out, ring_counter_1_o3);
  or or_1 (Load_MAR, Enable_PC, _1_out, _2_out, _3_out);
  and _3 (_3_out, SUB_out, ring_counter_1_o3);
  and _4 (_4_out, LDA_out, ring_counter_1_o4);
  and _5 (_5_out, ADD_out, ring_counter_1_o4);
  or or_2 (Enable_ROM, Load_IR, _4_out, _5_out, _6_out);
  and _6 (_6_out, SUB_out, ring_counter_1_o4);
  and _8 (_8_out, ADD_out, ring_counter_1_o3);
  and _7 (_7_out, LDA_out, ring_counter_1_o3);
  or or_3 (Enable_IR, _7_out, _8_out, _9_out);
  and _9 (_9_out, SUB_out, ring_counter_1_o3);
  and _10 (_10_out, LDA_out, ring_counter_1_o4);
  and _12 (_12_out, SUB_out, ring_counter_1_o5);
  and _11 (_11_out, ADD_out, ring_counter_1_o5);
  or or_4 (Load_A, _10_out, _11_out, _12_out);
  and _13 (Enable_A, OUT_out, ring_counter_1_o3);
  and _14 (Subtract, SUB_out, ring_counter_1_o5);
  and _16 (_16_out, SUB_out, ring_counter_1_o5);
  and _15 (_15_out, ADD_out, ring_counter_1_o5);
  or or_5 (Enable_ALU, _15_out, _16_out);
  and _17 (_17_out, ADD_out, ring_counter_1_o4);
  and _18 (_18_out, SUB_out, ring_counter_1_o4);
  or or_6 (Load_B, _17_out, _18_out);
  and _19 (Load_O, OUT_out, ring_counter_1_o3);

  assign CLR = Clear;
endmodule

module IR (
  input  I7,
  input  I6,
  input  I5,
  input  I4,
  input  I3,
  input  I2,
  input  I1,
  input  I0,
  input  L,
  input  CLK,
  input  CLR,
  input  E,
  output O7,
  output O6,
  output O5,
  output O4,
  output O3,
  output O2,
  output O1,
  output O0
);

  wire and_1_out, and_2_out, and_3_out, and_4_out, and_5_out, and_6_out, and_7_out, and_8_out, and_9_out,
       and_10_out, and_11_out, and_12_out, and_13_out, and_14_out, and_15_out, and_16_out, d_ff_5_q,
       d_ff_6_q, d_ff_7_q, d_ff_8_q, not_1_out, or_1_out, or_2_out, or_3_out, or_4_out, or_5_out, or_6_out,
       or_7_out, or_8_out;

  and and_1 (and_1_out, not_1_out, O7);
  and and_2 (and_2_out, L, I7);
  or or_1 (or_1_out, and_2_out, and_1_out);
  and and_3 (and_3_out, not_1_out, O6);
  and and_4 (and_4_out, L, I6);
  or or_2 (or_2_out, and_4_out, and_3_out);
  D_Flip_Flop d_ff_1 (.clk(CLK), .D(or_1_out), .Q(O7), .reset(CLR));  // open: Qn, preset, en
  and and_5 (and_5_out, L, I5);
  and and_6 (and_6_out, not_1_out, O5);
  or or_3 (or_3_out, and_5_out, and_6_out);
  D_Flip_Flop d_ff_2 (.clk(CLK), .D(or_2_out), .Q(O6), .reset(CLR));  // open: Qn, preset, en
  and and_7 (and_7_out, L, I4);
  and and_8 (and_8_out, not_1_out, O4);
  or or_4 (or_4_out, and_7_out, and_8_out);
  D_Flip_Flop d_ff_3 (.clk(CLK), .D(or_3_out), .Q(O5), .reset(CLR));  // open: Qn, preset, en
  and and_9 (and_9_out, L, I3);
  and and_10 (and_10_out, not_1_out, d_ff_5_q);
  or or_5 (or_5_out, and_9_out, and_10_out);
  D_Flip_Flop d_ff_4 (.clk(CLK), .D(or_4_out), .Q(O4), .reset(CLR));  // open: Qn, preset, en
  and and_11 (and_11_out, L, I2);
  and and_12 (and_12_out, not_1_out, d_ff_6_q);
  or or_6 (or_6_out, and_11_out, and_12_out);
  D_Flip_Flop d_ff_5 (.clk(CLK), .D(or_5_out), .Q(d_ff_5_q), .reset(CLR));  // open: Qn, preset, en
  assign O3 = E ? d_ff_5_q : 1'bz;  // Controlled_Buffer controlled_buffer_1
  and and_13 (and_13_out, not_1_out, d_ff_7_q);
  and and_14 (and_14_out, L, I1);
  or or_7 (or_7_out, and_14_out, and_13_out);
  D_Flip_Flop d_ff_6 (.clk(CLK), .D(or_6_out), .Q(d_ff_6_q), .reset(CLR));  // open: Qn, preset, en
  assign O2 = E ? d_ff_6_q : 1'bz;  // Controlled_Buffer controlled_buffer_2
  and and_15 (and_15_out, L, I0);
  and and_16 (and_16_out, not_1_out, d_ff_8_q);
  or or_8 (or_8_out, and_15_out, and_16_out);
  D_Flip_Flop d_ff_7 (.clk(CLK), .D(or_7_out), .Q(d_ff_7_q), .reset(CLR));  // open: Qn, preset, en
  assign O1 = E ? d_ff_7_q : 1'bz;  // Controlled_Buffer controlled_buffer_3
  not not_1 (not_1_out, L);
  D_Flip_Flop d_ff_8 (.clk(CLK), .D(or_8_out), .Q(d_ff_8_q), .reset(CLR));  // open: Qn, preset, en
  assign O0 = E ? d_ff_8_q : 1'bz;  // Controlled_Buffer controlled_buffer_4
endmodule

module ROM (
  input  E,
  input  A3,
  input  A2,
  input  A1,
  input  A0,
  output O7,
  output O6,
  output O5,
  output O4,
  output O3,
  output O2,
  output O1,
  output O0
);

  wire and_1_out, and_2_out, and_3_out, and_4_out, and_5_out, and_6_out, and_7_out, and_8_out, and_9_out,
       and_10_out, and_11_out, and_12_out, and_13_out, and_14_out, and_15_out, and_16_out,
       controlled_buffer_1_out, controlled_buffer_2_out, controlled_buffer_33_out, controlled_buffer_34_out,
       controlled_buffer_65_out, controlled_buffer_66_out, controlled_buffer_67_out,
       controlled_buffer_115_out, not_1_out, not_2_out, not_3_out, not_4_out;

  not not_1 (not_1_out, A3);
  not not_2 (not_2_out, A2);
  not not_3 (not_3_out, A1);
  not not_4 (not_4_out, A0);
  and and_1 (and_1_out, not_4_out, not_3_out, not_2_out, not_1_out);
  and and_2 (and_2_out, A0, not_3_out, not_2_out, not_1_out);
  and and_3 (and_3_out, not_4_out, A1, not_2_out, not_1_out);
  and and_4 (and_4_out, A0, A1, not_2_out, not_1_out);
  and and_5 (and_5_out, not_4_out, not_3_out, A2, not_1_out);
  and and_6 (and_6_out, A0, not_3_out, A2, not_1_out);
  and and_7 (and_7_out, not_4_out, A1, A2, not_1_out);
  and and_8 (and_8_out, A0, A1, A2, not_1_out);
  and and_9 (and_9_out, not_4_out, not_3_out, not_2_out, A3);
  and and_10 (and_10_out, A0, not_3_out, not_2_out, A3);
  and and_11 (and_11_out, not_4_out, A1, not_2_out, A3);
  and and_12 (and_12_out, A0, A1, not_2_out, A3);
  and and_13 (and_13_out, not_4_out, not_3_out, A2, A3);
  and and_14 (and_14_out, A0, not_3_out, A2, A3);
  and and_15 (and_15_out, not_4_out, A1, A2, A3);
  and and_16 (and_16_out, A0, A1, A2, A3);
  assign controlled_buffer_1_out = and_1_out ? 1'b0 : 1'bz;  // Controlled_Buffer controlled_buffer_1
  assign controlled_buffer_2_out = and_1_out ? 1'b0 : 1'bz;  // Controlled_Buffer controlled_buffer_2
  assign controlled_buffer_1_out = and_2_out ? 1'b0 : 1'bz;  // Controlled_Buffer controlled_buffer_3
  assign controlled_buffer_2_out = and_2_out ? 1'b0 : 1'bz;  // Controlled_Buffer controlled_buffer_4
  assign controlled_buffer_2_out = and_3_out ? 1'b1 : 1'bz;  // Controlled_Buffer controlled_buffer_5
  assign controlled_buffer_1_out = and_3_out ? 1'b1 : 1'bz;  // Controlled_Buffer controlled_buffer_6
  assign controlled_buffer_1_out = and_4_out ? 1'b1 : 1'bz;  // Controlled_Buffer controlled_buffer_7
  assign controlled_buffer_2_out = and_4_out ? 1'b1 : 1'bz;  // Controlled_Buffer controlled_buffer_8
  assign controlled_buffer_2_out = and_5_out ? 1'b0 : 1'bz;  // Controlled_Buffer controlled_buffer_9
  assign controlled_buffer_1_out = and_5_out ? 1'b0 : 1'bz;  // Controlled_Buffer controlled_buffer_10
  assign controlled_buffer_2_out = and_6_out ? 1'b0 : 1'bz;  // Controlled_Buffer controlled_buffer_11
  assign controlled_buffer_1_out = and_6_out ? 1'b0 : 1'bz;  // Controlled_Buffer controlled_buffer_12
  assign controlled_buffer_1_out = and_7_out ? 1'b0 : 1'bz;  // Controlled_Buffer controlled_buffer_13
  assign controlled_buffer_2_out = and_7_out ? 1'b0 : 1'bz;  // Controlled_Buffer controlled_buffer_14
  assign controlled_buffer_1_out = and_8_out ? 1'b0 : 1'bz;  // Controlled_Buffer controlled_buffer_15
  assign controlled_buffer_2_out = and_8_out ? 1'b0 : 1'bz;  // Controlled_Buffer controlled_buffer_16
  assign controlled_buffer_1_out = and_9_out ? 1'b0 : 1'bz;  // Controlled_Buffer controlled_buffer_17
  assign controlled_buffer_2_out = and_9_out ? 1'b0 : 1'bz;  // Controlled_Buffer controlled_buffer_18
  assign controlled_buffer_2_out = and_10_out ? 1'b0 : 1'bz;  // Controlled_Buffer controlled_buffer_19
  assign controlled_buffer_1_out = and_10_out ? 1'b0 : 1'bz;  // Controlled_Buffer controlled_buffer_20
  assign controlled_buffer_1_out = and_11_out ? 1'b0 : 1'bz;  // Controlled_Buffer controlled_buffer_21
  assign controlled_buffer_2_out = and_11_out ? 1'b0 : 1'bz;  // Controlled_Buffer controlled_buffer_22
  assign controlled_buffer_1_out = and_12_out ? 1'b0 : 1'bz;  // Controlled_Buffer controlled_buffer_23
  assign controlled_buffer_2_out = and_12_out ? 1'b0 : 1'bz;  // Controlled_Buffer controlled_buffer_24
  assign controlled_buffer_2_out = and_13_out ? 1'b0 : 1'bz;  // Controlled_Buffer controlled_buffer_25
  assign controlled_buffer_1_out = and_13_out ? 1'b0 : 1'bz;  // Controlled_Buffer controlled_buffer_26
  assign controlled_buffer_1_out = and_14_out ? 1'b0 : 1'bz;  // Controlled_Buffer controlled_buffer_27
  assign controlled_buffer_2_out = and_14_out ? 1'b0 : 1'bz;  // Controlled_Buffer controlled_buffer_28
  assign controlled_buffer_1_out = and_15_out ? 1'b0 : 1'bz;  // Controlled_Buffer controlled_buffer_29
  assign controlled_buffer_2_out = and_15_out ? 1'b0 : 1'bz;  // Controlled_Buffer controlled_buffer_30
  assign controlled_buffer_1_out = and_16_out ? 1'b0 : 1'bz;  // Controlled_Buffer controlled_buffer_31
  assign controlled_buffer_2_out = and_16_out ? 1'b0 : 1'bz;  // Controlled_Buffer controlled_buffer_32
  assign controlled_buffer_33_out = and_1_out ? 1'b0 : 1'bz;  // Controlled_Buffer controlled_buffer_33
  assign controlled_buffer_34_out = and_1_out ? 1'b0 : 1'bz;  // Controlled_Buffer controlled_buffer_34
  assign controlled_buffer_33_out = and_2_out ? 1'b0 : 1'bz;  // Controlled_Buffer controlled_buffer_35
  assign controlled_buffer_34_out = and_2_out ? 1'b1 : 1'bz;  // Controlled_Buffer controlled_buffer_36
  assign controlled_buffer_34_out = and_3_out ? 1'b1 : 1'bz;  // Controlled_Buffer controlled_buffer_37
  assign controlled_buffer_33_out = and_3_out ? 1'b0 : 1'bz;  // Controlled_Buffer controlled_buffer_38
  assign controlled_buffer_34_out = and_4_out ? 1'b1 : 1'bz;  // Controlled_Buffer controlled_buffer_39
  assign controlled_buffer_33_out = and_4_out ? 1'b1 : 1'bz;  // Controlled_Buffer controlled_buffer_40
  assign controlled_buffer_34_out = and_5_out ? 1'b0 : 1'bz;  // Controlled_Buffer controlled_buffer_41
  assign controlled_buffer_33_out = and_5_out ? 1'b0 : 1'bz;  // Controlled_Buffer controlled_buffer_42
  assign controlled_buffer_34_out = and_6_out ? 1'b0 : 1'bz;  // Controlled_Buffer controlled_buffer_43
  assign controlled_buffer_33_out = and_6_out ? 1'b0 : 1'bz;  // Controlled_Buffer controlled_buffer_44
  assign controlled_buffer_33_out = and_7_out ? 1'b0 : 1'bz;  // Controlled_Buffer controlled_buffer_45
  assign controlled_buffer_34_out = and_7_out ? 1'b0 : 1'bz;  // Controlled_Buffer controlled_buffer_46
  assign controlled_buffer_33_out = and_8_out ? 1'b0 : 1'bz;  // Controlled_Buffer controlled_buffer_47
  assign controlled_buffer_34_out = and_8_out ? 1'b0 : 1'bz;  // Controlled_Buffer controlled_buffer_48
  assign controlled_buffer_33_out = and_9_out ? 1'b0 : 1'bz;  // Controlled_Buffer controlled_buffer_49
  assign controlled_buffer_34_out = and_9_out ? 1'b0 : 1'bz;  // Controlled_Buffer controlled_buffer_50
  assign controlled_buffer_33_out = and_10_out ? 1'b0 : 1'bz;  // Controlled_Buffer controlled_buffer_51
  assign controlled_buffer_34_out = and_10_out ? 1'b0 : 1'bz;  // Controlled_Buffer controlled_buffer_52
  assign controlled_buffer_33_out = and_11_out ? 1'b0 : 1'bz;  // Controlled_Buffer controlled_buffer_53
  assign controlled_buffer_34_out = and_11_out ? 1'b0 : 1'bz;  // Controlled_Buffer controlled_buffer_54
  assign controlled_buffer_34_out = and_12_out ? 1'b0 : 1'bz;  // Controlled_Buffer controlled_buffer_55
  assign controlled_buffer_33_out = and_12_out ? 1'b0 : 1'bz;  // Controlled_Buffer controlled_buffer_56
  assign controlled_buffer_34_out = and_13_out ? 1'b0 : 1'bz;  // Controlled_Buffer controlled_buffer_57
  assign controlled_buffer_33_out = and_13_out ? 1'b0 : 1'bz;  // Controlled_Buffer controlled_buffer_58
  assign controlled_buffer_33_out = and_14_out ? 1'b0 : 1'bz;  // Controlled_Buffer controlled_buffer_59
  assign controlled_buffer_34_out = and_14_out ? 1'b0 : 1'bz;  // Controlled_Buffer controlled_buffer_60
  assign controlled_buffer_33_out = and_15_out ? 1'b0 : 1'bz;  // Controlled_Buffer controlled_buffer_61
  assign controlled_buffer_34_out = and_15_out ? 1'b0 : 1'bz;  // Controlled_Buffer controlled_buffer_62
  assign controlled_buffer_33_out = and_16_out ? 1'b0 : 1'bz;  // Controlled_Buffer controlled_buffer_63
  assign controlled_buffer_34_out = and_16_out ? 1'b0 : 1'bz;  // Controlled_Buffer controlled_buffer_64
  assign controlled_buffer_65_out = and_1_out ? 1'b0 : 1'bz;  // Controlled_Buffer controlled_buffer_65
  assign controlled_buffer_66_out = and_1_out ? 1'b0 : 1'bz;  // Controlled_Buffer controlled_buffer_66
  assign controlled_buffer_67_out = and_1_out ? 1'b1 : 1'bz;  // Controlled_Buffer controlled_buffer_67
  assign controlled_buffer_66_out = and_2_out ? 1'b0 : 1'bz;  // Controlled_Buffer controlled_buffer_68
  assign controlled_buffer_67_out = and_2_out ? 1'b1 : 1'bz;  // Controlled_Buffer controlled_buffer_69
  assign controlled_buffer_65_out = and_2_out ? 1'b0 : 1'bz;  // Controlled_Buffer controlled_buffer_70
  assign controlled_buffer_67_out = and_3_out ? 1'b0 : 1'bz;  // Controlled_Buffer controlled_buffer_71
  assign controlled_buffer_66_out = and_3_out ? 1'b0 : 1'bz;  // Controlled_Buffer controlled_buffer_72
  assign controlled_buffer_65_out = and_3_out ? 1'b0 : 1'bz;  // Controlled_Buffer controlled_buffer_73
  assign controlled_buffer_65_out = and_4_out ? 1'b0 : 1'bz;  // Controlled_Buffer controlled_buffer_74
  assign controlled_buffer_67_out = and_4_out ? 1'b0 : 1'bz;  // Controlled_Buffer controlled_buffer_75
  assign controlled_buffer_66_out = and_4_out ? 1'b0 : 1'bz;  // Controlled_Buffer controlled_buffer_76
  assign controlled_buffer_67_out = and_5_out ? 1'b1 : 1'bz;  // Controlled_Buffer controlled_buffer_77
  assign controlled_buffer_66_out = and_5_out ? 1'b1 : 1'bz;  // Controlled_Buffer controlled_buffer_78
  assign controlled_buffer_65_out = and_5_out ? 1'b1 : 1'bz;  // Controlled_Buffer controlled_buffer_79
  assign controlled_buffer_65_out = and_6_out ? 1'b0 : 1'bz;  // Controlled_Buffer controlled_buffer_80
  assign controlled_buffer_67_out = and_6_out ? 1'b1 : 1'bz;  // Controlled_Buffer controlled_buffer_81
  assign controlled_buffer_66_out = and_6_out ? 1'b1 : 1'bz;  // Controlled_Buffer controlled_buffer_82
  assign controlled_buffer_66_out = and_7_out ? 1'b0 : 1'bz;  // Controlled_Buffer controlled_buffer_83
  assign controlled_buffer_67_out = and_7_out ? 1'b0 : 1'bz;  // Controlled_Buffer controlled_buffer_84
  assign controlled_buffer_65_out = and_7_out ? 1'b0 : 1'bz;  // Controlled_Buffer controlled_buffer_85
  assign controlled_buffer_65_out = and_8_out ? 1'b0 : 1'bz;  // Controlled_Buffer controlled_buffer_86
  assign controlled_buffer_66_out = and_8_out ? 1'b0 : 1'bz;  // Controlled_Buffer controlled_buffer_87
  assign controlled_buffer_67_out = and_8_out ? 1'b0 : 1'bz;  // Controlled_Buffer controlled_buffer_88
  assign controlled_buffer_66_out = and_9_out ? 1'b0 : 1'bz;  // Controlled_Buffer controlled_buffer_89
  assign controlled_buffer_67_out = and_9_out ? 1'b0 : 1'bz;  // Controlled_Buffer controlled_buffer_90
  assign controlled_buffer_65_out = and_9_out ? 1'b0 : 1'bz;  // Controlled_Buffer controlled_buffer_91
  assign controlled_buffer_65_out = and_10_out ? 1'b0 : 1'bz;  // Controlled_Buffer controlled_buffer_92
  assign controlled_buffer_66_out = and_10_out ? 1'b0 : 1'bz;  // Controlled_Buffer controlled_buffer_93
  assign controlled_buffer_67_out = and_10_out ? 1'b0 : 1'bz;  // Controlled_Buffer controlled_buffer_94
  assign controlled_buffer_65_out = and_11_out ? 1'b0 : 1'bz;  // Controlled_Buffer controlled_buffer_95
  assign controlled_buffer_67_out = and_11_out ? 1'b0 : 1'bz;  // Controlled_Buffer controlled_buffer_96
  assign controlled_buffer_66_out = and_11_out ? 1'b0 : 1'bz;  // Controlled_Buffer controlled_buffer_97
  assign controlled_buffer_66_out = and_12_out ? 1'b0 : 1'bz;  // Controlled_Buffer controlled_buffer_98
  assign controlled_buffer_67_out = and_12_out ? 1'b0 : 1'bz;  // Controlled_Buffer controlled_buffer_99
  assign controlled_buffer_65_out = and_12_out ? 1'b0 : 1'bz;  // Controlled_Buffer controlled_buffer_100
  assign controlled_buffer_66_out = and_13_out ? 1'b0 : 1'bz;  // Controlled_Buffer controlled_buffer_101
  assign controlled_buffer_65_out = and_13_out ? 1'b0 : 1'bz;  // Controlled_Buffer controlled_buffer_102
  assign controlled_buffer_67_out = and_13_out ? 1'b0 : 1'bz;  // Controlled_Buffer controlled_buffer_103
  assign controlled_buffer_66_out = and_14_out ? 1'b0 : 1'bz;  // Controlled_Buffer controlled_buffer_104
  assign controlled_buffer_67_out = and_14_out ? 1'b0 : 1'bz;  // Controlled_Buffer controlled_buffer_105
  assign controlled_buffer_65_out = and_14_out ? 1'b0 : 1'bz;  // Controlled_Buffer controlled_buffer_106
  assign controlled_buffer_66_out = and_15_out ? 1'b0 : 1'bz;  // Controlled_Buffer controlled_buffer_107
  assign controlled_buffer_67_out = and_15_out ? 1'b0 : 1'bz;  // Controlled_Buffer controlled_buffer_108
  assign controlled_buffer_65_out = and_15_out ? 1'b0 : 1'bz;  // Controlled_Buffer controlled_buffer_109
  assign controlled_buffer_65_out = and_16_out ? 1'b0 : 1'bz;  // Controlled_Buffer controlled_buffer_110
  assign controlled_buffer_66_out = and_16_out ? 1'b0 : 1'bz;  // Controlled_Buffer controlled_buffer_111
  assign controlled_buffer_67_out = and_16_out ? 1'b0 : 1'bz;  // Controlled_Buffer controlled_buffer_112
  assign O7 = E ? controlled_buffer_1_out : 1'bz;  // Controlled_Buffer controlled_buffer_113
  assign O6 = E ? controlled_buffer_2_out : 1'bz;  // Controlled_Buffer controlled_buffer_114
  assign controlled_buffer_115_out = and_1_out ? 1'b0 : 1'bz;  // Controlled_Buffer controlled_buffer_115
  assign controlled_buffer_115_out = and_2_out ? 1'b1 : 1'bz;  // Controlled_Buffer controlled_buffer_116
  assign controlled_buffer_115_out = and_3_out ? 1'b0 : 1'bz;  // Controlled_Buffer controlled_buffer_117
  assign controlled_buffer_115_out = and_4_out ? 1'b0 : 1'bz;  // Controlled_Buffer controlled_buffer_118
  assign controlled_buffer_115_out = and_5_out ? 1'b1 : 1'bz;  // Controlled_Buffer controlled_buffer_119
  assign controlled_buffer_115_out = and_6_out ? 1'b1 : 1'bz;  // Controlled_Buffer controlled_buffer_120
  assign controlled_buffer_115_out = and_7_out ? 1'b0 : 1'bz;  // Controlled_Buffer controlled_buffer_121
  assign controlled_buffer_115_out = and_8_out ? 1'b0 : 1'bz;  // Controlled_Buffer controlled_buffer_122
  assign controlled_buffer_115_out = and_9_out ? 1'b0 : 1'bz;  // Controlled_Buffer controlled_buffer_123
  assign controlled_buffer_115_out = and_10_out ? 1'b0 : 1'bz;  // Controlled_Buffer controlled_buffer_124
  assign controlled_buffer_115_out = and_11_out ? 1'b0 : 1'bz;  // Controlled_Buffer controlled_buffer_125
  assign controlled_buffer_115_out = and_12_out ? 1'b0 : 1'bz;  // Controlled_Buffer controlled_buffer_126
  assign controlled_buffer_115_out = and_13_out ? 1'b0 : 1'bz;  // Controlled_Buffer controlled_buffer_127
  assign controlled_buffer_115_out = and_14_out ? 1'b0 : 1'bz;  // Controlled_Buffer controlled_buffer_128
  assign controlled_buffer_115_out = and_15_out ? 1'b0 : 1'bz;  // Controlled_Buffer controlled_buffer_129
  assign controlled_buffer_115_out = and_16_out ? 1'b0 : 1'bz;  // Controlled_Buffer controlled_buffer_130
  assign O2 = E ? controlled_buffer_67_out : 1'bz;  // Controlled_Buffer controlled_buffer_131
  assign O3 = E ? controlled_buffer_65_out : 1'bz;  // Controlled_Buffer controlled_buffer_132
  assign O5 = E ? controlled_buffer_34_out : 1'bz;  // Controlled_Buffer controlled_buffer_133
  assign O4 = E ? controlled_buffer_33_out : 1'bz;  // Controlled_Buffer controlled_buffer_134
  assign O1 = E ? controlled_buffer_66_out : 1'bz;  // Controlled_Buffer controlled_buffer_135
  assign O0 = E ? controlled_buffer_115_out : 1'bz;  // Controlled_Buffer controlled_buffer_136
endmodule

module MAR (
  input  I3,
  input  I2,
  input  I1,
  input  I0,
  input  L,
  input  CLK,
  input  CLR,
  output O3,
  output O2,
  output O1,
  output O0
);

  wire and_1_out, and_2_out, and_3_out, and_4_out, and_5_out, and_6_out, and_7_out, and_8_out, not_1_out,
       or_1_out, or_2_out, or_3_out, or_4_out;

  and and_1 (and_1_out, L, I3);
  and and_2 (and_2_out, not_1_out, O3);
  or or_1 (or_1_out, and_1_out, and_2_out);
  and and_3 (and_3_out, L, I2);
  and and_4 (and_4_out, not_1_out, O2);
  or or_2 (or_2_out, and_3_out, and_4_out);
  D_Flip_Flop d_ff_1 (.clk(CLK), .D(or_1_out), .Q(O3), .reset(CLR));  // open: Qn, preset, en
  and and_5 (and_5_out, L, I1);
  and and_6 (and_6_out, not_1_out, O1);
  or or_3 (or_3_out, and_5_out, and_6_out);
  D_Flip_Flop d_ff_2 (.clk(CLK), .D(or_2_out), .Q(O2), .reset(CLR));  // open: Qn, preset, en
  and and_7 (and_7_out, not_1_out, O0);
  and and_8 (and_8_out, L, I0);
  or or_4 (or_4_out, and_8_out, and_7_out);
  D_Flip_Flop d_ff_3 (.clk(CLK), .D(or_3_out), .Q(O1), .reset(CLR));  // open: Qn, preset, en
  not not_1 (not_1_out, L);
  D_Flip_Flop d_ff_4 (.clk(CLK), .D(or_4_out), .Q(O0), .reset(CLR));  // open: Qn, preset, en
endmodule

module PC (
  input  C,
  input  CLK,
  input  CLR,
  input  E,
  output O3,
  output O2,
  output O1,
  output O0
);

  wire and_1_out, and_2_out, and_3_out, j_k_ff_1_q, j_k_ff_2_q, j_k_ff_3_q, j_k_ff_4_q;

  and and_1 (and_1_out, j_k_ff_2_q, j_k_ff_3_q, j_k_ff_4_q, C);
  and and_2 (and_2_out, j_k_ff_3_q, j_k_ff_4_q, C);
  J_K_Flip_Flop j_k_ff_1 (
    .J(and_1_out), .clk(CLK), .K(and_1_out), .Q(j_k_ff_1_q), .reset(CLR));  // open: Qn, preset, en
  assign O3 = E ? j_k_ff_1_q : 1'bz;  // Controlled_Buffer controlled_buffer_1
  and and_3 (and_3_out, j_k_ff_4_q, C);
  J_K_Flip_Flop j_k_ff_2 (
    .J(and_2_out), .clk(CLK), .K(and_2_out), .Q(j_k_ff_2_q), .reset(CLR));  // open: Qn, preset, en
  assign O2 = E ? j_k_ff_2_q : 1'bz;  // Controlled_Buffer controlled_buffer_2
  J_K_Flip_Flop j_k_ff_3 (
    .J(and_3_out), .clk(CLK), .K(and_3_out), .Q(j_k_ff_3_q), .reset(CLR));  // open: Qn, preset, en
  assign O1 = E ? j_k_ff_3_q : 1'bz;  // Controlled_Buffer controlled_buffer_3
  J_K_Flip_Flop j_k_ff_4 (.J(C), .clk(CLK), .K(C), .Q(j_k_ff_4_q), .reset(CLR));  // open: Qn, preset, en
  assign O0 = E ? j_k_ff_4_q : 1'bz;  // Controlled_Buffer controlled_buffer_4
endmodule

module Ring_Counter (
  input  CLK,
  input  CLR,
  output O5,
  output O4,
  output O3,
  output O2,
  output O1,
  output O0
);

  D_Flip_Flop d_ff_1 (.clk(CLK), .D(O4), .Q(O5), .reset(CLR));  // open: Qn, preset, en
  D_Flip_Flop d_ff_2 (.clk(CLK), .D(O3), .Q(O4), .reset(CLR));  // open: Qn, preset, en
  D_Flip_Flop d_ff_3 (.clk(CLK), .D(O2), .Q(O3), .reset(CLR));  // open: Qn, preset, en
  D_Flip_Flop d_ff_4 (.clk(CLK), .D(O1), .Q(O2), .reset(CLR));  // open: Qn, preset, en
  D_Flip_Flop d_ff_5 (.clk(CLK), .D(O0), .Q(O1), .reset(CLR));  // open: Qn, preset, en
  D_Flip_Flop d_ff_6 (.clk(CLK), .D(O5), .Q(O0), .preset(CLR));  // open: Qn, en, reset
endmodule
